# Fritzing sketch vco-level-2 (saved by Fritzing 0.9.4)
breadboards: 1

parts:
  U1 = LM358 [package=dip08]
  R1 = Resistor [tolerance=±5% resistance=100k package=THT]
  R2 = Resistor [tolerance=±5% resistance=56k package=THT]
  Q1 = NPN-Transistor [package="TO92 [THT]"]
  R3 = Resistor [tolerance=±5% resistance=56k package=THT]
  R4 = Resistor [tolerance=±5% resistance=100k package=THT]
  R6 = Resistor [tolerance=±5% resistance=56k package=THT]
  R7 = Resistor [tolerance=±5% resistance=100k package=THT]
  R8 = Resistor [tolerance=±5% resistance=100k package=THT]
  R5 = Resistor [tolerance=±5% resistance=100k package=THT]

nets:
  N1: U1.G$1_OUT, U1.G$2_-IN
  N2: U1.G$1_-IN, R1.Pin_1, Q1.E
  N3: U1.G$1_+IN, R2.Pin_1, R3.Pin_1
  N4: U1.G$2_+IN, R6.Pin_1, R5.Pin_1
  N5: U1.G$2_OUT, R4.Pin_0, R5.Pin_0
  N6: U1.G$1_V+, R8.Pin_0
  N7: Q1.B, R4.Pin_1
  N8: Q1.C, R3.Pin_0
  N9: R7.Pin_1, R8.Pin_1
